# Fritzing sketch smart-humidifier (saved by Fritzing 0.9.10b)
breadboards: 1

parts:
  Part1 = Photon
  C1 = Ceramic Capacitor [capacitance=100nF voltage=35V package="100 mil [THT, multilayer]"]  # not connected
  C2 = Ceramic Capacitor [capacitance=100nF voltage=35V package="100 mil [THT, multilayer]"]  # not connected
  C3 = Ceramic Capacitor [capacitance=10µF voltage=35V package="100 mil [THT, multilayer]"]
  C4 = Ceramic Capacitor [capacitance=10µF voltage=35V package="100 mil [THT, multilayer]"]
  DHT1 = Humidity and Temperature Sensor DHT11
  R1 = Resistor [tolerance=±5% power=0.25 resistance=10k package=THT]
  J1 = Basic Servo

nets:
  GND: Part1.GND, C3.0, C4.0, J1.gnd
  VIN: Part1.VIN, C3.1, DHT1.Vcc, DHT1.GND_2, R1.Pin_1
  N1: Part1.D1, J1.pulse
  N2: Part1.D2, DHT1.Data-signal, R1.Pin_0
  3V3: Part1.3V3, C4.1, J1.vcc

custom parts:
  Humidity and Temperature Sensor DHT11: Digital relative humidity & temperature sensor DHT11
